# Fritzing sketch DPV Controller Redesign2 (saved by Fritzing 0.9.2b)
circuit board: 12.18cm x 12.18cm
breadboards: 1

parts:
  MCU = Arduino Pro Mini v13
  OUT- = female pin header, 1 pin [form="♀ (female)"]
  IN+ = female pin header, 1 pin [form="♀ (female)"]
  IN- = female pin header, 1 pin [form="♀ (female)"]
  OUT+ = rounded female pin header, 1 pin [form="♀ (female rounded)"]
  IPP100N06SL2 = Basic FET N-Channel [package="TO220 [THT]"]
  IPP100N06SL2_2 = Basic FET N-Channel [package="TO220 [THT]"]
  R1 = Resistor [tolerance=±5% resistance=0.01 package=THT]
  R2 = Resistor [tolerance=±5% resistance=0.01 package=THT]
  POWER_DIODES = pnp-Powertransistor [package="TO220 [THT]"]
  Pad5 = Pad [width=16.6789957918051 height=9.30689557253599 connect=center]
  Pad4 = Pad [width=18.5268002104228 height=8.17636964208456 connect=center]
  Pad2 = Pad [width=12.3171049856035 height=23.1008966378738 connect=center]
  Pad3 = Pad [width=7.90222222222222 height=9.03111111111111 connect=center]  # not connected
  R4 = Resistor [tolerance=±5% resistance=5.6k package=THT]
  R5 = Resistor [tolerance=±5% resistance=39k package=THT]
  R6 = Resistor [tolerance=±5% resistance=5.6k package=THT]
  C1 = Electrolytic Capacitor [capacitance=470µF voltage=16V package="200 mil [THT, electrolytic]"]
  C2 = Electrolytic Capacitor [capacitance=470µF voltage=16V package="200 mil [THT, electrolytic]"]
  IPP100N06SL2_3 = Basic FET N-Channel [package="TO220 [THT]"]
  Spare_1 = molex pin header, 2 pins [form=molex]
  Spare_2 = molex pin header, 2 pins [form=molex]
  Trigger = molex pin header, 2 pins [form=molex]
  Buzzer = molex pin header, 2 pins [form=molex]
  Pad6 = Pad [width=10.4047590953786 height=11.4087708947886 connect=center]  # not connected
  Pad7 = Pad [width=5.977167220769263 height=9.7551679105299236 connect=center]  # not connected
  R7 = Resistor [tolerance=±5% resistance=10k package=THT]
  BCP56_(BH) = TRANSISTOR_NPN [package=sot223]
  R8 = Resistor [tolerance=±5% resistance=1k package=THT]
  R3 = Resistor [tolerance=±5% resistance=39k package=THT]
  BCP53 = TRANSISTOR_NPN [package=sot223]

nets:
  GND: MCU.GND, OUT-.pin1, IN-.pin1, R1.Pin_0, R2.Pin_0, Pad5.pad, R4.Pin_1, R6.Pin_0, C1.-, C2.-, IPP100N06SL2_3.source, Spare_1.pin2, Spare_2.pin2, Trigger.pin2, R8.Pin_0, BCP53.C
  6V: MCU.RAW, OUT+.pin1, BCP56_(BH).C
  5V: MCU.VCC
  N1: MCU.A3, Spare_2.pin1
  N2: MCU.A2, Spare_1.pin1
  N3: MCU.A1, R4.Pin_0, R3.Pin_0
  N4: MCU.A0, R5.Pin_1, R6.Pin_1
  N5: MCU.D6_PWM, R7.Pin_0
  N6: MCU.D3_PWM, IPP100N06SL2_3.gate
  N7: MCU.D2, Trigger.pin1
  43.8V/Motor +: IN+.pin1, POWER_DIODES.collector, Pad2.pad, R5.Pin_0, C1.+, C2.+, Buzzer.pin1
  N8: IPP100N06SL2.gate, IPP100N06SL2_2.gate, BCP56_(BH).E, R8.Pin_1, BCP53.E
  Motor -: IPP100N06SL2.drain, IPP100N06SL2_2.drain, POWER_DIODES.base, POWER_DIODES.emitter
  N9: IPP100N06SL2.source, IPP100N06SL2_2.source, R1.Pin_1, R2.Pin_1, Pad4.pad, R3.Pin_1
  N10: IPP100N06SL2_3.drain, Buzzer.pin2
  N11: R7.Pin_1, BCP56_(BH).B, BCP53.B

notes:
  Voltage Regulator Module
